# Fritzing sketch pianoDiagram (saved by Fritzing 0.8.7b)
breadboards: 1

parts:
  Part1 = Arduino MP3 Player Shield
  Intel(R)_Galileo_1 = Intel(R) Galileo  # not connected
  MCP23S1 = MCP23S17 [package="28-pin PDIP"]
  LED1 = LED - 5mm [color="Red (633nm)" package="5 mm [THT]"]
  LED2 = LED - 5mm [color="Red (633nm)" package="5 mm [THT]"]
  LED3 = LED - 5mm [color="Red (633nm)" package="5 mm [THT]"]
  LED4 = LED - 5mm [color="Red (633nm)" package="5 mm [THT]"]
  LED5 = LED - 5mm [color="Red (633nm)" package="5 mm [THT]"]
  LED6 = LED - 5mm [color="Red (633nm)" package="5 mm [THT]"]
  LED8 = LED - 5mm [color="Red (633nm)" package="5 mm [THT]"]
  LED10 = LED - 5mm [color="Red (633nm)" package="5 mm [THT]"]
  LED11 = LED - 5mm [color="Red (633nm)" package="5 mm [THT]"]
  LED12 = LED - 5mm [color="Red (633nm)" package="5 mm [THT]"]
  LED13 = LED - 5mm [color="Red (633nm)" package="5 mm [THT]"]
  LED14 = LED - 5mm [color="Red (633nm)" package="5 mm [THT]"]
  LED15 = LED - 5mm [color="Red (633nm)" package="5 mm [THT]"]
  LED16 = LED - 5mm [color="Red (633nm)" package="5 mm [THT]"]
  LED17 = LED - 5mm [color="Red (633nm)" package="5 mm [THT]"]
  LED18 = LED - 5mm [color="Red (633nm)" package="5 mm [THT]"]

nets:
  N1: Part1.3.3, MCP23S1.V_dd, MCP23S1.RESET
  N2: Part1.D10, MCP23S1.CS
  N3: Part1.5V-MOSI, MCP23S1.SI
  N4: Part1.5V-SCK, MCP23S1.SCK
  N5: Part1.GND, MCP23S1.V_ss, MCP23S1.A0, MCP23S1.A1, MCP23S1.A2, LED1.anode, LED2.anode, LED3.anode, LED4.anode, LED6.anode, LED8.anode, LED10.anode, LED11.anode, LED12.anode, LED13.anode, LED14.anode, LED16.anode, LED17.anode, LED18.anode
  N6: MCP23S1.GPB0, LED11.cathode
  N7: MCP23S1.GPB1, LED12.cathode
  N8: MCP23S1.GPB2, LED13.cathode
  N9: MCP23S1.GPB3, LED14.cathode
  N10: MCP23S1.GPB4, LED15.cathode
  N11: MCP23S1.GPB5, LED16.cathode
  N12: MCP23S1.GPB6, LED17.cathode
  N13: MCP23S1.GPB7, LED18.cathode
  N14: MCP23S1.GPA0, LED10.cathode
  N15: MCP23S1.GPA1, LED8.cathode
  N16: MCP23S1.GPA2, LED6.cathode
  N17: MCP23S1.GPA3, LED5.cathode
  N18: MCP23S1.GPA4, LED4.cathode
  N19: MCP23S1.GPA5, LED3.cathode
  N20: MCP23S1.GPA6, LED2.cathode
  N21: MCP23S1.GPA7, LED1.cathode

custom parts:
  Intel(R) Galileo: Galileo is a microcontroller board based on the Intel® Quark SoC X1000 Application Processor, a 32-bit Intel Pentium-class system on a chip (datasheet). It’s the first board based on Intel® architecture designed to be hardware and software pin-compatible with Arduino shields designed for the Uno R3. Digital pins 0 to 13 (and the adjacent AREF and GND pins), Analog inputs 0 to 5, the power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
  MCP23S17: 16-bit input/output port expander with interrupt output Cascadable for up to 8 devices on one bus 25mA sink/source capability per I/O Supports up to 10MHz SPI™ clock speeds
